# Fritzing sketch circuit_ver2 (saved by Fritzing 0.9.5d)
circuit board: 5.3cm x 3.2cm
breadboards: 1

parts:
  Arduino_nano_33_BLE = Arduino Nano 33 BLE Sense
  LiPo_1S_330mAh = LIPO-110mAh [package=lipo-110]
  FET_K401x_2 = Basic FET N-Channel [package="TO220 [THT]"]
  FET_K401x_3 = Basic FET N-Channel [package="TO220 [THT]"]
  M3 = DC Motor
  Diode3 = Schottky Diode [package="300 mil [THT]"]
  FET_K401x_4 = Basic FET N-Channel [package="TO220 [THT]"]
  M4 = DC Motor
  Diode4 = Schottky Diode [package="300 mil [THT]"]
  C4 = Ceramic Capacitor [capacitance=47µF voltage=20V package="200 mil [THT, multilayer]"]
  VL53L0X1 = VL53L0X ToF laser distance sensor [package=THT]
  R4_2 = Resistor [tolerance=±5% resistance=10k package=THT]
  R1-2 = Resistor [tolerance=±5% resistance=10k package=THT]
  R2_2 = Resistor [tolerance=±5% resistance=10k package=THT]
  Diode1 = Schottky Diode [part_number=1N5817 package="300 mil [THT]"]
  Diode2 = Schottky Diode [part_number=1N5817 package="300 mil [THT]"]
  M2 = DC Motor
  M1 = DC Motor
  R2_1 = Resistor [tolerance=±5% resistance=100 package=THT]
  R1_1 = Resistor [tolerance=±5% resistance=100 package=THT]
  R3_1 = Resistor [tolerance=±5% resistance=100 package=THT]
  R4_1 = Resistor [tolerance=±5% resistance=100 package=THT]
  R3_2 = Resistor [tolerance=±5% resistance=10k package=THT]
  C3 = Ceramic Capacitor [capacitance=47µF voltage=20V package="200 mil [THT, multilayer]"]
  C2 = Ceramic Capacitor [capacitance=47µF voltage=20V package="200 mil [THT, multilayer]"]
  C1 = Ceramic Capacitor [capacitance=47µF voltage=20V package="200 mil [THT, multilayer]"]
  FET_K401x_1 = Basic FET N-Channel [package="TO220 [THT]"]
  電圧レギュレータのダミー = Pololu S9V11F5

nets:
  GND: Arduino_nano_33_BLE.GND, LiPo_1S_330mAh.-, FET_K401x_2.source, FET_K401x_3.source, FET_K401x_4.source, C4.0, VL53L0X1.GND, R4_2.Pin_1, R1-2.Pin_1, R2_2.Pin_1, R3_2.Pin_1, C3.0, C2.0, C1.0, FET_K401x_1.source, 電圧レギュレータのダミー.Pin_2
  N1: Arduino_nano_33_BLE.D4, VL53L0X1.G
  N2: Arduino_nano_33_BLE.D5~, R1_1.Pin_0
  N3: Arduino_nano_33_BLE.D6~, R2_1.Pin_0
  N4: Arduino_nano_33_BLE.D7, R3_1.Pin_0
  N5: Arduino_nano_33_BLE.D8, R4_1.Pin_0
  VIN: Arduino_nano_33_BLE.VIN, VL53L0X1.VIN, 電圧レギュレータのダミー.Pin_3
  N6: Arduino_nano_33_BLE.A5, VL53L0X1.SCL
  N7: Arduino_nano_33_BLE.A4, VL53L0X1.SDA
  N8: LiPo_1S_330mAh.+, M3.pin_1, Diode3.cathode, M4.pin_1, Diode4.cathode, C4.1, Diode1.cathode, Diode2.cathode, M2.pin_1, M1.pin_1, C3.1, C2.1, C1.1, 電圧レギュレータのダミー.Pin_1
  N9: FET_K401x_2.gate, R2_2.Pin_0, R2_1.Pin_1
  N10: FET_K401x_2.drain, Diode2.anode, M2.pin_2
  N11: FET_K401x_3.gate, R3_1.Pin_1, R3_2.Pin_0
  N12: FET_K401x_3.drain, M3.pin_2, Diode3.anode
  N13: FET_K401x_4.gate, R4_2.Pin_0, R4_1.Pin_1
  N14: FET_K401x_4.drain, M4.pin_2, Diode4.anode
  N15: R1-2.Pin_0, R1_1.Pin_1, FET_K401x_1.gate
  N16: Diode1.anode, M1.pin_2, FET_K401x_1.drain

notes:
  モータ駆動部
  電圧レギュレータ
  測距センサ

custom parts:
  Arduino Nano 33 BLE Sense: The Nano 33 BLE Sense (without headers) is Arduino’s 3.3V AI enabled board in the smallest available form factor: 45x18mm! The Arduino Nano 33 BLE Sense is a completely new board on a well-known form factor. It comes with a series of embedded sensors: 9 axis inertial sensor: what makes this board ideal for wearable devices humidity, and temperature sensor: to get highly accurate measurements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
  VL53L0X ToF laser distance sensor: Time of Flight laser distance sensor VL53L0X.
  Pololu S9V11F5: The S9V11x family of efficient switching regulators (also called switched-mode power supplies (SMPS) or DC-to-DC converters) use a buck-boost topology to convert both higher and lower input voltages to a regulated output voltage.
